# Fritzing sketch esp8622-01_dev_board_pcb (saved by Fritzing 0.9.1b)
circuit board: 3.7cm x 3.7cm
breadboards: 1

parts:
  R1 = Resistor [tolerance=±5% resistance=2.2k package=THT]
  R2 = Resistor [tolerance=±5% resistance=2.2k package=THT]
  R3 = Resistor [tolerance=±5% resistance=2.2k package=THT]
  R4 = Resistor [tolerance=±5% resistance=2.2k package=THT]
  J1 = female pin header, 4 pins [form="♀ (female)"]
  J2 = female pin header, 4 pins [form="♀ (female)"]
  SW_RST = Round Pushbutton
  SW_GPIO0 = Round Pushbutton
  GPIO2_OUT = male pin header, 1 pin [form="♂ (male)"]
  GPIO0_OUT = male pin header, 1 pin [form="♂ (male)"]
  VCC = rounded female pin header, 1 pin [form="♀ (female rounded)"]
  USB_TXT = male pin header, 1 pin [form="♂ (male)"]
  USB_RX = male pin header, 1 pin [form="♂ (male)"]
  USB_GND = male pin header, 1 pin [form="♂ (male)"]
  GND = male pin header, 1 pin [form="♂ (male)"]
  J3 = male pin header, 10 pins [form="♂ (male)"]  # not connected
  J4 = male pin header, 10 pins [form="♂ (male)"]  # not connected

nets:
  N1: R1.Pin_0, J1.pin3, SW_RST.leg0
  5V: R1.Pin_1, R2.Pin_1, R3.Pin_1, R4.Pin_1, J1.pin4, VCC.pin1
  N2: R2.Pin_0, J1.pin2
  N3: R3.Pin_0, J2.pin3, SW_GPIO0.leg1, GPIO0_OUT.pin1
  N4: R4.Pin_0, J2.pin2, GPIO2_OUT.pin1
  N5: J1.pin1, USB_RX.pin1
  GND: J2.pin1, SW_RST.leg1, SW_GPIO0.leg0, USB_GND.pin1, GND.pin1
  N6: J2.pin4, USB_TXT.pin1

notes:
  VCC
  GND
  usb GND
  usb TX
  usb RX
  TX
  CH_PD
  RST
  GPIO2
  GPIO0
  RX
